# Fritzing sketch 02-preemptive-led-wiring-diagram (saved by Fritzing 0.9.6b)
breadboards: 1

parts:
  J1 = STM32 Nucleo boards
  LED1 = smd LED [color="Red (633nm)" package="0603 [SMD]"]
  R1 = Resistor [tolerance=±5% resistance=220 package="0402 [SMD]"]
  R2 = Resistor [tolerance=±5% resistance=220 package="0402 [SMD]"]
  LED2 = smd LED [color="Green (555nm)" package="0603 [SMD]"]

nets:
  N1: J1.D2, LED2.cathode
  N2: J1.D4, LED1.cathode
  N3: J1.3V3, R1.Pin_1, R2.Pin_1
  N4: LED1.anode, R2.Pin_0
  N5: R1.Pin_0, LED2.anode
